// Logisim project MorseCodeEncoder.circ as structural Verilog
module Combinational (
  input  A,
  input  B,
  input  C,
  input  D,
  input  E,
  output aout,
  output bout,
  output cout,
  output dout,
  output eout,
  output fout,
  output gout,
  output hout,
  output iout,
  output jout
);

  wire and_1_out, and_2_out, and_3_out, and_4_out, and_5_out, and_6_out, and_7_out, and_8_out, and_9_out,
       and_10_out, and_11_out, and_12_out, and_13_out, and_14_out, and_15_out, and_16_out, and_17_out,
       and_18_out, and_19_out, and_20_out, and_21_out, and_22_out, and_23_out, and_24_out, and_25_out,
       and_26_out, and_27_out, and_28_out, and_29_out, and_30_out, and_31_out, and_32_out, and_33_out,
       and_34_out, and_35_out, and_36_out, and_37_out, and_38_out, and_39_out, and_40_out, and_41_out,
       and_42_out, and_43_out, and_44_out, and_45_out, and_46_out, and_47_out, and_48_out, and_49_out,
       and_50_out, and_51_out, and_52_out, and_53_out, and_54_out, and_55_out, and_56_out, and_57_out,
       and_58_out, and_59_out, and_60_out, and_61_out, and_62_out, and_63_out, and_64_out, and_65_out,
       and_66_out, and_67_out, and_68_out, and_69_out, and_70_out, and_71_out, and_72_out, and_73_out,
       and_74_out, and_75_out, and_76_out, and_77_out, and_78_out, and_79_out, and_80_out, and_81_out,
       and_82_out, and_83_out, and_84_out, and_85_out, and_86_out, and_87_out, and_88_out, and_89_out,
       and_90_out, and_91_out, and_92_out, and_93_out, and_94_out, and_95_out, and_96_out, and_97_out,
       and_98_out, and_99_out, and_100_out, and_101_out, and_102_out, and_103_out, and_104_out, and_105_out,
       and_106_out, and_107_out, and_108_out, and_109_out, and_110_out, and_111_out, and_112_out,
       and_113_out, and_114_out, and_115_out, and_116_out, and_117_out, and_118_out, and_119_out,
       and_120_out, and_121_out, and_122_out, and_123_out, and_124_out, and_125_out, and_126_out,
       and_127_out, and_128_out, and_129_out, and_130_out, not_1_out, not_2_out, not_3_out, not_4_out,
       not_5_out, or_1_out, or_2_out, or_3_out, or_4_out, or_5_out, or_6_out, or_7_out, or_8_out, or_9_out,
       or_10_out, or_11_out, or_12_out, or_13_out, or_14_out, or_15_out, or_16_out, or_17_out, or_18_out,
       or_19_out, or_20_out, or_21_out, or_22_out, or_23_out, or_24_out, or_25_out, or_26_out, or_27_out,
       or_28_out, or_29_out, or_30_out, or_31_out, or_32_out, or_36_out, or_38_out;

  not not_1 (not_1_out, A);
  not not_2 (not_2_out, B);
  not not_3 (not_3_out, C);
  not not_4 (not_4_out, D);
  not not_5 (not_5_out, E);
  and and_1 (and_1_out, not_1_out, D);
  and and_2 (and_2_out, B, C);
  and and_3 (and_3_out, B, C);
  and and_4 (and_4_out, A, not_3_out);
  and and_5 (and_5_out, not_4_out, E);
  and and_6 (and_6_out, not_2_out, C);
  and and_7 (and_7_out, not_4_out, not_5_out);
  and and_8 (and_8_out, not_1_out, not_3_out);
  and and_9 (and_9_out, A, C);
  and and_10 (and_10_out, not_2_out, C);
  and and_11 (and_11_out, D, not_5_out);
  and and_12 (and_12_out, not_1_out, B);
  and and_13 (and_13_out, not_3_out, not_5_out);
  and and_14 (and_14_out, A, not_2_out);
  and and_15 (and_15_out, not_3_out, not_5_out);
  and and_16 (and_16_out, A, not_2_out);
  and and_17 (and_17_out, C, D);
  and and_18 (and_18_out, not_1_out, not_3_out);
  and and_19 (and_19_out, not_4_out, not_5_out);
  and and_20 (and_20_out, A, B);
  and and_21 (and_21_out, B, C);
  and and_22 (and_22_out, A, not_2_out);
  and and_23 (and_23_out, not_3_out, E);
  and and_24 (and_24_out, A, not_2_out);
  and and_25 (and_25_out, not_4_out, E);
  and and_26 (and_26_out, not_2_out, C);
  and and_27 (and_27_out, D, not_5_out);
  and and_28 (and_28_out, not_1_out, not_3_out);
  and and_29 (and_29_out, not_1_out, not_2_out);
  and and_30 (and_30_out, A, C);
  and and_31 (and_31_out, A, B);
  and and_32 (and_32_out, not_1_out, D);
  and and_33 (and_33_out, A, C);
  and and_34 (and_34_out, not_1_out, B);
  and and_35 (and_35_out, not_3_out, not_5_out);
  and and_36 (and_36_out, A, not_3_out);
  and and_37 (and_37_out, not_4_out, E);
  and and_38 (and_38_out, A, B);
  and and_39 (and_39_out, not_4_out, not_5_out);
  and and_40 (and_40_out, B, C);
  and and_41 (and_41_out, not_4_out, not_5_out);
  and and_42 (and_42_out, not_1_out, not_2_out);
  and and_43 (and_43_out, not_1_out, B);
  and and_44 (and_44_out, and_1_out, E);
  and and_45 (and_45_out, and_2_out, E);
  and and_46 (and_46_out, and_3_out, D);
  and and_47 (and_47_out, and_4_out, and_5_out);
  and and_48 (and_48_out, A, B);
  and and_49 (and_49_out, and_6_out, and_7_out);
  and and_50 (and_50_out, not_1_out, not_2_out);
  and and_51 (and_51_out, not_3_out, not_5_out);
  and and_52 (and_52_out, and_8_out, not_4_out);
  and and_53 (and_53_out, and_9_out, E);
  and and_54 (and_54_out, and_10_out, and_11_out);
  and and_55 (and_55_out, and_12_out, and_13_out);
  and and_56 (and_56_out, and_14_out, and_15_out);
  and and_57 (and_57_out, and_16_out, D);
  and and_58 (and_58_out, not_1_out, B);
  and and_59 (and_59_out, not_4_out, not_5_out);
  and and_60 (and_60_out, B, C);
  and and_61 (and_61_out, and_17_out, E);
  and and_62 (and_62_out, not_1_out, not_2_out);
  and and_63 (and_63_out, not_1_out, not_2_out);
  and and_64 (and_64_out, not_4_out, not_5_out);
  and and_65 (and_65_out, not_1_out, not_3_out);
  and and_66 (and_66_out, not_2_out, not_3_out);
  and and_67 (and_67_out, not_2_out, not_3_out);
  and and_68 (and_68_out, A, not_3_out);
  and and_69 (and_69_out, A, not_3_out);
  and and_70 (and_70_out, and_18_out, and_19_out);
  and and_71 (and_71_out, and_20_out, D);
  and and_72 (and_72_out, and_21_out, E);
  and and_73 (and_73_out, and_22_out, and_23_out);
  and and_74 (and_74_out, and_24_out, and_25_out);
  and and_75 (and_75_out, and_26_out, and_27_out);
  and and_76 (and_76_out, not_1_out, not_2_out);
  and and_77 (and_77_out, C, D);
  and and_78 (and_78_out, and_28_out, D);
  and and_79 (and_79_out, and_29_out, not_5_out);
  and and_80 (and_80_out, not_2_out, not_3_out);
  and and_81 (and_81_out, and_30_out, E);
  and and_82 (and_82_out, and_31_out, not_4_out);
  and and_83 (and_83_out, not_1_out, C);
  and and_84 (and_84_out, not_4_out, not_5_out);
  and and_85 (and_85_out, and_32_out, E);
  and and_86 (and_86_out, and_33_out, D);
  and and_87 (and_87_out, A, not_2_out);
  and and_88 (and_88_out, not_3_out, not_4_out);
  and and_89 (and_89_out, and_34_out, and_35_out);
  and and_90 (and_90_out, and_36_out, and_37_out);
  and and_91 (and_91_out, B, not_3_out);
  and and_92 (and_92_out, and_38_out, and_39_out);
  and and_93 (and_93_out, and_40_out, and_41_out);
  and and_94 (and_94_out, B, C);
  and and_95 (and_95_out, D, E);
  and and_96 (and_96_out, not_1_out, not_2_out);
  and and_97 (and_97_out, D, not_5_out);
  and and_98 (and_98_out, not_2_out, C);
  and and_99 (and_99_out, D, not_5_out);
  and and_100 (and_100_out, A, not_3_out);
  and and_101 (and_101_out, and_42_out, not_3_out);
  and and_102 (and_102_out, D, E);
  and and_103 (and_103_out, A, not_3_out);
  and and_104 (and_104_out, not_4_out, E);
  and and_105 (and_105_out, and_43_out, not_3_out);
  and and_106 (and_106_out, D, not_5_out);
  or or_1 (or_1_out, and_44_out, and_45_out);
  or or_2 (or_2_out, and_46_out, and_47_out);
  or or_3 (or_3_out, and_48_out, and_49_out);
  and and_107 (and_107_out, and_50_out, and_51_out);
  or or_4 (or_4_out, and_52_out, and_53_out);
  or or_5 (or_5_out, and_54_out, and_55_out);
  or or_6 (or_6_out, and_56_out, and_57_out);
  and and_108 (and_108_out, and_58_out, and_59_out);
  or or_7 (or_7_out, and_60_out, and_61_out);
  and and_109 (and_109_out, and_62_out, not_3_out);
  and and_110 (and_110_out, and_63_out, and_64_out);
  and and_111 (and_111_out, and_65_out, D);
  and and_112 (and_112_out, and_66_out, not_4_out);
  and and_113 (and_113_out, and_67_out, not_5_out);
  and and_114 (and_114_out, and_68_out, not_4_out);
  and and_115 (and_115_out, and_69_out, not_5_out);
  or or_8 (or_8_out, and_70_out, and_71_out);
  or or_9 (or_9_out, and_72_out, and_73_out);
  or or_10 (or_10_out, and_74_out, and_75_out);
  and and_116 (and_116_out, and_76_out, and_77_out);
  or or_11 (or_11_out, and_78_out, and_79_out);
  and and_117 (and_117_out, and_80_out, not_5_out);
  or or_12 (or_12_out, and_81_out, and_82_out);
  and and_118 (and_118_out, and_83_out, and_84_out);
  or or_13 (or_13_out, and_85_out, and_86_out);
  and and_119 (and_119_out, and_87_out, and_88_out);
  or or_14 (or_14_out, and_89_out, and_90_out);
  and and_120 (and_120_out, and_91_out, D);
  or or_15 (or_15_out, and_92_out, and_93_out);
  and and_121 (and_121_out, and_94_out, and_95_out);
  and and_122 (and_122_out, and_96_out, and_97_out);
  and and_123 (and_123_out, and_98_out, and_99_out);
  and and_124 (and_124_out, and_100_out, not_4_out);
  and and_125 (and_125_out, and_101_out, and_102_out);
  and and_126 (and_126_out, B, not_3_out);
  and and_127 (and_127_out, D, not_5_out);
  and and_128 (and_128_out, and_103_out, and_104_out);
  and and_129 (and_129_out, and_105_out, and_106_out);
  or or_16 (or_16_out, or_1_out, or_2_out);
  or or_17 (or_17_out, or_3_out, and_107_out);
  or or_18 (or_18_out, or_4_out, or_5_out);
  or or_19 (or_19_out, or_6_out, and_108_out);
  or or_20 (or_20_out, or_7_out, and_109_out);
  or or_21 (or_21_out, and_110_out, and_111_out);
  or or_22 (or_22_out, and_112_out, and_113_out);
  or or_23 (or_23_out, and_114_out, and_115_out);
  or or_24 (or_24_out, or_8_out, or_9_out);
  or or_25 (or_25_out, or_10_out, and_116_out);
  or or_26 (or_26_out, or_11_out, and_117_out);
  or or_27 (or_27_out, or_12_out, and_118_out);
  or or_28 (or_28_out, or_13_out, and_119_out);
  or or_29 (or_29_out, or_14_out, and_120_out);
  or or_30 (or_30_out, or_15_out, and_121_out);
  or or_31 (or_31_out, and_122_out, and_123_out);
  or or_32 (or_32_out, and_124_out, and_125_out);
  and and_130 (and_130_out, and_126_out, and_127_out);
  or or_33 (jout, and_128_out, and_129_out);
  or or_34 (bout, or_16_out, or_17_out);
  or or_35 (cout, or_18_out, or_19_out);
  or or_36 (or_36_out, or_20_out, or_21_out);
  or or_37 (dout, or_36_out, or_38_out);
  or or_38 (or_38_out, or_22_out, or_23_out);
  or or_39 (eout, or_24_out, or_25_out);
  or or_40 (fout, or_26_out, or_27_out);
  or or_41 (gout, or_28_out, or_29_out);
  or or_42 (hout, or_30_out, or_31_out);
  or or_43 (iout, or_32_out, and_130_out);

  assign aout = 1'b1;
endmodule

module CombinationalFromEq (
  input  A,
  input  B,
  input  C,
  input  D,
  input  E,
  output aout,
  output bout,
  output cout,
  output dout,
  output eout,
  output fout,
  output gout,
  output hout,
  output iout,
  output jout
);

  wire and_1_out, and_2_out, and_3_out, and_4_out, and_5_out, and_6_out, and_7_out, and_8_out, and_9_out,
       and_10_out, and_11_out, and_12_out, and_13_out, and_14_out, and_15_out, and_16_out, and_17_out,
       and_18_out, and_19_out, and_20_out, and_21_out, and_22_out, and_23_out, and_24_out, and_25_out,
       and_26_out, and_27_out, and_28_out, and_29_out, and_30_out, and_31_out, and_32_out, and_33_out,
       and_34_out, and_35_out, and_36_out, and_37_out, and_38_out, and_39_out, and_40_out, and_41_out,
       and_42_out, and_43_out, and_44_out, and_45_out, and_46_out, and_47_out, and_48_out, and_49_out,
       and_50_out, and_51_out, and_52_out, and_53_out, and_54_out, and_55_out, and_56_out, and_57_out,
       and_58_out, and_59_out, and_60_out, and_61_out, and_62_out, and_63_out, and_64_out, and_65_out,
       and_66_out, and_67_out, and_68_out, and_69_out, and_70_out, and_71_out, and_72_out, and_73_out,
       and_74_out, and_75_out, and_76_out, and_77_out, and_78_out, and_79_out, and_80_out, and_81_out,
       and_82_out, and_83_out, and_84_out, and_85_out, and_86_out, and_87_out, and_88_out, and_89_out,
       and_90_out, and_91_out, and_92_out, and_93_out, and_94_out, and_95_out, and_96_out, and_97_out,
       and_98_out, and_99_out, and_100_out, and_101_out, and_102_out, and_103_out, and_104_out, and_105_out,
       and_106_out, and_107_out, and_108_out, and_109_out, and_110_out, and_111_out, and_112_out,
       and_113_out, and_114_out, and_115_out, and_116_out, and_117_out, and_118_out, and_119_out,
       and_120_out, and_121_out, and_122_out, and_123_out, and_124_out, not_1_out, not_2_out, not_3_out,
       not_4_out, not_5_out, or_1_out, or_2_out, or_3_out, or_4_out, or_5_out, or_6_out, or_7_out, or_8_out,
       or_9_out, or_10_out, or_11_out, or_12_out, or_13_out, or_14_out, or_15_out, or_16_out, or_17_out,
       or_18_out, or_19_out, or_20_out, or_21_out, or_22_out, or_23_out, or_24_out, or_25_out, or_26_out,
       or_27_out, or_28_out, or_29_out, or_30_out, or_31_out, or_32_out;

  not not_1 (not_1_out, A);
  not not_2 (not_2_out, B);
  not not_3 (not_3_out, C);
  not not_4 (not_4_out, D);
  not not_5 (not_5_out, E);
  and and_1 (and_1_out, not_1_out, D);
  and and_2 (and_2_out, B, C);
  and and_3 (and_3_out, B, C);
  and and_4 (and_4_out, not_1_out, not_2_out);
  and and_5 (and_5_out, not_3_out, D);
  and and_6 (and_6_out, not_2_out, C);
  and and_7 (and_7_out, not_4_out, not_5_out);
  and and_8 (and_8_out, A, not_2_out);
  and and_9 (and_9_out, not_1_out, not_3_out);
  and and_10 (and_10_out, A, C);
  and and_11 (and_11_out, not_2_out, C);
  and and_12 (and_12_out, D, not_5_out);
  and and_13 (and_13_out, not_1_out, B);
  and and_14 (and_14_out, not_3_out, not_5_out);
  and and_15 (and_15_out, not_1_out, B);
  and and_16 (and_16_out, not_4_out, not_5_out);
  and and_17 (and_17_out, not_3_out, D);
  and and_18 (and_18_out, A, not_3_out);
  and and_19 (and_19_out, not_1_out, not_2_out);
  and and_20 (and_20_out, C, D);
  and and_21 (and_21_out, B, C);
  and and_22 (and_22_out, A, B);
  and and_23 (and_23_out, not_1_out, not_2_out);
  and and_24 (and_24_out, C, D);
  and and_25 (and_25_out, not_2_out, C);
  and and_26 (and_26_out, D, not_5_out);
  and and_27 (and_27_out, A, not_2_out);
  and and_28 (and_28_out, not_3_out, E);
  and and_29 (and_29_out, A, not_2_out);
  and and_30 (and_30_out, not_4_out, E);
  and and_31 (and_31_out, not_1_out, not_3_out);
  and and_32 (and_32_out, not_1_out, not_2_out);
  and and_33 (and_33_out, A, C);
  and and_34 (and_34_out, A, B);
  and and_35 (and_35_out, not_1_out, D);
  and and_36 (and_36_out, B, not_3_out);
  and and_37 (and_37_out, A, B);
  and and_38 (and_38_out, not_1_out, B);
  and and_39 (and_39_out, not_3_out, not_5_out);
  and and_40 (and_40_out, not_1_out, not_2_out);
  and and_41 (and_41_out, D, not_5_out);
  and and_42 (and_42_out, not_2_out, C);
  and and_43 (and_43_out, D, not_5_out);
  and and_44 (and_44_out, A, not_3_out);
  and and_45 (and_45_out, B, not_3_out);
  and and_46 (and_46_out, D, not_5_out);
  and and_47 (and_47_out, not_1_out, not_2_out);
  and and_48 (and_48_out, not_1_out, B);
  and and_49 (and_49_out, A, B);
  and and_50 (and_50_out, and_1_out, E);
  and and_51 (and_51_out, and_2_out, E);
  and and_52 (and_52_out, and_3_out, D);
  and and_53 (and_53_out, and_4_out, and_5_out);
  and and_54 (and_54_out, and_6_out, and_7_out);
  and and_55 (and_55_out, A, not_3_out);
  and and_56 (and_56_out, not_4_out, E);
  and and_57 (and_57_out, and_8_out, D);
  and and_58 (and_58_out, and_9_out, not_4_out);
  and and_59 (and_59_out, and_10_out, E);
  and and_60 (and_60_out, and_11_out, and_12_out);
  and and_61 (and_61_out, and_13_out, and_14_out);
  and and_62 (and_62_out, and_15_out, and_16_out);
  and and_63 (and_63_out, A, not_2_out);
  and and_64 (and_64_out, not_3_out, not_5_out);
  and and_65 (and_65_out, B, D);
  and and_66 (and_66_out, B, C);
  and and_67 (and_67_out, and_17_out, not_5_out);
  and and_68 (and_68_out, and_18_out, not_4_out);
  and and_69 (and_69_out, and_19_out, not_3_out);
  and and_70 (and_70_out, and_20_out, E);
  and and_71 (and_71_out, not_1_out, C);
  and and_72 (and_72_out, not_4_out, not_5_out);
  and and_73 (and_73_out, and_21_out, E);
  and and_74 (and_74_out, and_22_out, D);
  and and_75 (and_75_out, and_23_out, and_24_out);
  and and_76 (and_76_out, and_25_out, and_26_out);
  and and_77 (and_77_out, and_27_out, and_28_out);
  and and_78 (and_78_out, and_29_out, and_30_out);
  and and_79 (and_79_out, not_1_out, not_3_out);
  and and_80 (and_80_out, not_4_out, not_5_out);
  and and_81 (and_81_out, and_31_out, D);
  and and_82 (and_82_out, and_32_out, not_5_out);
  and and_83 (and_83_out, not_2_out, not_3_out);
  and and_84 (and_84_out, and_33_out, E);
  and and_85 (and_85_out, and_34_out, not_4_out);
  and and_86 (and_86_out, not_1_out, C);
  and and_87 (and_87_out, not_4_out, not_5_out);
  and and_88 (and_88_out, and_35_out, E);
  and and_89 (and_89_out, and_36_out, D);
  and and_90 (and_90_out, A, C);
  and and_91 (and_91_out, and_37_out, E);
  and and_92 (and_92_out, and_38_out, and_39_out);
  and and_93 (and_93_out, A, not_2_out);
  and and_94 (and_94_out, not_3_out, not_4_out);
  and and_95 (and_95_out, and_40_out, and_41_out);
  and and_96 (and_96_out, and_42_out, and_43_out);
  and and_97 (and_97_out, B, C);
  and and_98 (and_98_out, not_4_out, not_5_out);
  and and_99 (and_99_out, B, C);
  and and_100 (and_100_out, D, E);
  and and_101 (and_101_out, A, B);
  and and_102 (and_102_out, not_4_out, not_5_out);
  and and_103 (and_103_out, and_44_out, not_4_out);
  and and_104 (and_104_out, and_45_out, and_46_out);
  and and_105 (and_105_out, and_47_out, not_3_out);
  and and_106 (and_106_out, D, E);
  and and_107 (and_107_out, A, not_3_out);
  and and_108 (and_108_out, not_4_out, E);
  and and_109 (and_109_out, and_48_out, not_3_out);
  and and_110 (and_110_out, D, not_5_out);
  or or_1 (or_1_out, and_49_out, and_50_out);
  or or_2 (or_2_out, and_51_out, and_52_out);
  or or_3 (or_3_out, and_53_out, and_54_out);
  and and_111 (and_111_out, and_55_out, and_56_out);
  or or_4 (or_4_out, and_57_out, and_58_out);
  or or_5 (or_5_out, and_59_out, and_60_out);
  or or_6 (or_6_out, and_61_out, and_62_out);
  and and_112 (and_112_out, and_63_out, and_64_out);
  or or_7 (or_7_out, and_65_out, and_66_out);
  or or_8 (or_8_out, and_67_out, and_68_out);
  or or_9 (or_9_out, and_69_out, and_70_out);
  and and_113 (and_113_out, and_71_out, and_72_out);
  or or_10 (or_10_out, and_73_out, and_74_out);
  or or_11 (or_11_out, and_75_out, and_76_out);
  or or_12 (or_12_out, and_77_out, and_78_out);
  and and_114 (and_114_out, and_79_out, and_80_out);
  or or_13 (or_13_out, and_81_out, and_82_out);
  and and_115 (and_115_out, and_83_out, not_5_out);
  or or_14 (or_14_out, and_84_out, and_85_out);
  and and_116 (and_116_out, and_86_out, and_87_out);
  or or_15 (or_15_out, and_88_out, and_89_out);
  and and_117 (and_117_out, and_90_out, D);
  or or_16 (or_16_out, and_91_out, and_92_out);
  and and_118 (and_118_out, and_93_out, and_94_out);
  or or_17 (or_17_out, and_95_out, and_96_out);
  and and_119 (and_119_out, and_97_out, and_98_out);
  and and_120 (and_120_out, and_99_out, and_100_out);
  and and_121 (and_121_out, and_101_out, and_102_out);
  or or_18 (or_18_out, and_103_out, and_104_out);
  and and_122 (and_122_out, and_105_out, and_106_out);
  and and_123 (and_123_out, and_107_out, and_108_out);
  and and_124 (and_124_out, and_109_out, and_110_out);
  or or_19 (or_19_out, or_1_out, or_2_out);
  or or_20 (or_20_out, or_3_out, and_111_out);
  or or_21 (or_21_out, or_4_out, or_5_out);
  or or_22 (or_22_out, or_6_out, and_112_out);
  or or_23 (or_23_out, or_7_out, or_8_out);
  or or_24 (or_24_out, or_9_out, and_113_out);
  or or_25 (or_25_out, or_10_out, or_11_out);
  or or_26 (or_26_out, or_12_out, and_114_out);
  or or_27 (or_27_out, or_13_out, and_115_out);
  or or_28 (or_28_out, or_14_out, and_116_out);
  or or_29 (or_29_out, or_15_out, and_117_out);
  or or_30 (or_30_out, or_16_out, and_118_out);
  or or_31 (or_31_out, or_17_out, and_119_out);
  or or_32 (or_32_out, and_120_out, and_121_out);
  or or_33 (iout, or_18_out, and_122_out);
  or or_34 (jout, and_123_out, and_124_out);
  or or_35 (bout, or_19_out, or_20_out);
  or or_36 (cout, or_21_out, or_22_out);
  or or_37 (dout, or_23_out, or_24_out);
  or or_38 (eout, or_25_out, or_26_out);
  or or_39 (fout, or_27_out, or_28_out);
  or or_40 (gout, or_29_out, or_30_out);
  or or_41 (hout, or_31_out, or_32_out);

  assign aout = 1'b1;
endmodule
